# Fritzing sketch Avionics Sketch (saved by Fritzing 0.9.3b)
breadboards: 1

parts:
  GPS_ProtoShield = Adafruit Ultimate GPS Logger Shield [part_number="Adafruit #1272"]
  Altitude_Sensor = Barometric Pressure Sensor - BMP180 Breakout (GY-68)
  IMU = InvenSense MPU6050
  Buzzer = Piezo Speaker
  Part4 = NRF24L01+ Breakout Board
  E-Match = LED - 3mm [color="Red (633nm)" package="3 mm [THT]"]

nets:
  VCC: GPS_ProtoShield.+5V, IMU.VCC, Part4.VCC
  GND: GPS_ProtoShield.GND, Altitude_Sensor.GND, IMU.GND, Buzzer.pin2, Part4.GND, E-Match.cathode
  N1: GPS_ProtoShield.D2, Buzzer.pin1
  N2: GPS_ProtoShield.D4, IMU.INT
  N3: GPS_ProtoShield.D7, Part4.CE
  N4: GPS_ProtoShield.D8, Part4.CS
  3.3V: GPS_ProtoShield.3.3V, Altitude_Sensor.VCC
  N5: GPS_ProtoShield.A1, E-Match.anode
  N6: GPS_ProtoShield.SCL, Altitude_Sensor.SCL, IMU.SCL
  N7: GPS_ProtoShield.SDA, Altitude_Sensor.SDA, IMU.SDA
  N8: GPS_ProtoShield.SCK, Part4.SCK
  N9: GPS_ProtoShield.MISO, Part4.MISO
  N10: GPS_ProtoShield.MOSI, Part4.MOSI

custom parts:
  Adafruit Ultimate GPS Logger Shield: Brand new and better than ever, we've replaced our Adafruit GPS shield kit with this assembled shield that comes with an Ultimate GPS module. This GPS shield works great with either UNO or Leonardo Arduinos and is designed to log data to an SD card. Or you can leave the SD card out and use the GPS for a geocaching project, or maybe a music player that changes tunes depending on where you are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
